// Logisim project 32RV.circ as structural Verilog
module main (
  input  [31:0] in_1,
  input  in_2
);

  wire clock_1_out, idecode_1_ar_i, idecode_1_ar_r, idecode_1_auipc, idecode_1_br, idecode_1_ebc,
       idecode_1_jal, idecode_1_jalr, idecode_1_ld, idecode_1_lui, idecode_1_st, not_1_out;
  wire [2:0] idecode_1_funct3;
  wire [4:0] idecode_1_rd, idecode_1_rs1, idecode_1_rs2;
  wire [6:0] idecode_1_funct7;
  wire [31:0] idecode_1_imm, IF_ID_q, IM_dout, multiplexer_1_out, programcounter_1_outpc,
       programcounter_1_outpcplus4;

  Multiplexer #(.width(32)) multiplexer_1 (
    .in0(in_1), .in1(programcounter_1_outpcplus4), .out(multiplexer_1_out), .sel(not_1_out));
  Clock clock_1 (.out(clock_1_out));
  not not_1 (not_1_out, in_2);
  ProgramCounter programcounter_1 (
    .inPC(multiplexer_1_out), .CLK(clock_1_out), .outPCPlus4(programcounter_1_outpcplus4),
    .outPC(programcounter_1_outpc));
  RAM #(.addrWidth(15), .dataWidth(32)) IM (
    .addr(programcounter_1_outpc[14:0]), .clk(clock_1_out), .dout(IM_dout));  // open: we, oe, din
  Register #(.width(32)) IF_ID (.D(IM_dout), .en(1'b1), .clk(clock_1_out), .Q(IF_ID_q));  // open: clr
  IDecode idecode_1 (
    .instr(IF_ID_q), .rd(idecode_1_rd), .funct3(idecode_1_funct3), .rs1(idecode_1_rs1), .rs2(idecode_1_rs2),
    .funct7(idecode_1_funct7), .imm(idecode_1_imm), .ar_r(idecode_1_ar_r), .ar_i(idecode_1_ar_i),
    .ld(idecode_1_ld), .st(idecode_1_st), .br(idecode_1_br), .jal(idecode_1_jal), .jalr(idecode_1_jalr),
    .lui(idecode_1_lui), .auipc(idecode_1_auipc), .ebc(idecode_1_ebc));

  // Other names for the same wires on the sheet: branch = in_2; jmp_ins_idx[31:0] = in_1
endmodule

module ProgramCounter (
  input  [31:0] inPC,
  input  CLK,
  output [31:0] outPCPlus4,
  output [31:0] outPC
);

  Register #(.width(32)) register_1 (.D(inPC), .en(1'b1), .clk(CLK), .Q(outPC));  // open: clr
  Adder #(.width(32)) adder_1 (.a(outPC), .b(32'h1), .out(outPCPlus4));  // open: cin, cout

  // Other names for the same wires on the sheet: CLK_t = CLK; inPC_t[31:0] = inPC; outPC_t[31:0] = outPC;
  //   outPCPlus4_t[31:0] = outPCPlus4
endmodule

module RegisterFile (
  input  [4:0] rsi1,
  input  [4:0] rsi2,
  input  [4:0] rdi,
  input  [31:0] rd,
  input  we,
  input  CLK,
  output [31:0] rs1,
  output [31:0] rs2
);

  wire x0we_t, x1we_t, x2we_t, x3we_t, x4we_t, x5we_t, x6we_t, x7we_t, x8we_t, x9we_t, x10we_t, x11we_t,
       x12we_t, x13we_t, x14we_t, x15we_t, x16we_t, x17we_t, x18we_t, x19we_t, x20we_t, x21we_t, x22we_t,
       x23we_t, x24we_t, x25we_t, x26we_t, x27we_t, x28we_t, x29we_t, x30we_t, x31we_t;
  wire [31:0] x1q_t, x2q_t, x3q_t, x4q_t, x5q_t, x6q_t, x7q_t, x8q_t, x9q_t, x10q_t, x11q_t, x12q_t, x13q_t,
       x14q_t, x15q_t, x16q_t, x17q_t, x18q_t, x19q_t, x20q_t, x21q_t, x22q_t, x23q_t, x24q_t, x25q_t,
       x26q_t, x27q_t, x28q_t, x29q_t, x30q_t, x31q_t;

  Demultiplexer #(.select(5)) demultiplexer_1 (
    .out0(x0we_t), .out1(x1we_t), .out2(x2we_t), .out3(x3we_t), .out4(x4we_t), .out5(x5we_t), .out6(x6we_t),
    .out7(x7we_t), .out8(x8we_t), .out9(x9we_t), .out10(x10we_t), .out11(x11we_t), .out12(x12we_t),
    .out13(x13we_t), .out14(x14we_t), .out15(x15we_t), .out16(x16we_t), .out17(x17we_t), .out18(x18we_t),
    .out19(x19we_t), .out20(x20we_t), .out21(x21we_t), .out22(x22we_t), .out23(x23we_t), .out24(x24we_t),
    .out25(x25we_t), .out26(x26we_t), .out27(x27we_t), .out28(x28we_t), .out29(x29we_t), .out30(x30we_t),
    .out31(x31we_t), .in(we), .sel(rdi));
  Register #(.width(32)) x4 (.D(rd), .en(x4we_t), .clk(CLK), .Q(x4q_t));  // open: clr
  Register #(.width(32)) x8 (.D(rd), .en(x8we_t), .clk(CLK), .Q(x8q_t));  // open: clr
  Register #(.width(32)) x12 (.D(rd), .en(x12we_t), .clk(CLK), .Q(x12q_t));  // open: clr
  Register #(.width(32)) x16 (.D(rd), .en(x16we_t), .clk(CLK), .Q(x16q_t));  // open: clr
  Register #(.width(32)) x20 (.D(rd), .en(x20we_t), .clk(CLK), .Q(x20q_t));  // open: clr
  Register #(.width(32)) x24 (.D(rd), .en(x24we_t), .clk(CLK), .Q(x24q_t));  // open: clr
  Register #(.width(32)) x28 (.D(rd), .en(x28we_t), .clk(CLK), .Q(x28q_t));  // open: clr
  Register #(.width(32)) x1 (.D(rd), .en(x1we_t), .clk(CLK), .Q(x1q_t));  // open: clr
  Register #(.width(32)) x5 (.D(rd), .en(x5we_t), .clk(CLK), .Q(x5q_t));  // open: clr
  Register #(.width(32)) x9 (.D(rd), .en(x9we_t), .clk(CLK), .Q(x9q_t));  // open: clr
  Register #(.width(32)) x13 (.D(rd), .en(x13we_t), .clk(CLK), .Q(x13q_t));  // open: clr
  Register #(.width(32)) x17 (.D(rd), .en(x17we_t), .clk(CLK), .Q(x17q_t));  // open: clr
  Register #(.width(32)) x21 (.D(rd), .en(x21we_t), .clk(CLK), .Q(x21q_t));  // open: clr
  Register #(.width(32)) x25 (.D(rd), .en(x25we_t), .clk(CLK), .Q(x25q_t));  // open: clr
  Register #(.width(32)) x29 (.D(rd), .en(x29we_t), .clk(CLK), .Q(x29q_t));  // open: clr
  Register #(.width(32)) x2 (.D(rd), .en(x2we_t), .clk(CLK), .Q(x2q_t));  // open: clr
  Register #(.width(32)) x6 (.D(rd), .en(x6we_t), .clk(CLK), .Q(x6q_t));  // open: clr
  Register #(.width(32)) x10 (.D(rd), .en(x10we_t), .clk(CLK), .Q(x10q_t));  // open: clr
  Register #(.width(32)) x14 (.D(rd), .en(x14we_t), .clk(CLK), .Q(x14q_t));  // open: clr
  Register #(.width(32)) x18 (.D(rd), .en(x18we_t), .clk(CLK), .Q(x18q_t));  // open: clr
  Register #(.width(32)) x22 (.D(rd), .en(x22we_t), .clk(CLK), .Q(x22q_t));  // open: clr
  Register #(.width(32)) x26 (.D(rd), .en(x26we_t), .clk(CLK), .Q(x26q_t));  // open: clr
  Register #(.width(32)) x30 (.D(rd), .en(x30we_t), .clk(CLK), .Q(x30q_t));  // open: clr
  Register #(.width(32)) x3 (.D(rd), .en(x3we_t), .clk(CLK), .Q(x3q_t));  // open: clr
  Register #(.width(32)) x7 (.D(rd), .en(x7we_t), .clk(CLK), .Q(x7q_t));  // open: clr
  Register #(.width(32)) x11 (.D(rd), .en(x11we_t), .clk(CLK), .Q(x11q_t));  // open: clr
  Register #(.width(32)) x15 (.D(rd), .en(x15we_t), .clk(CLK), .Q(x15q_t));  // open: clr
  Register #(.width(32)) x19 (.D(rd), .en(x19we_t), .clk(CLK), .Q(x19q_t));  // open: clr
  Register #(.width(32)) x23 (.D(rd), .en(x23we_t), .clk(CLK), .Q(x23q_t));  // open: clr
  Register #(.width(32)) x27 (.D(rd), .en(x27we_t), .clk(CLK), .Q(x27q_t));  // open: clr
  Register #(.width(32)) x31 (.D(rd), .en(x31we_t), .clk(CLK), .Q(x31q_t));  // open: clr
  Multiplexer #(.select(5), .width(32)) multiplexer_1 (
    .in0({32{1'b0}}), .in1(x1q_t), .in2(x2q_t), .in3(x3q_t), .in4(x4q_t), .in5(x5q_t), .in6(x6q_t),
    .in7(x7q_t), .in8(x8q_t), .in9(x9q_t), .in10(x10q_t), .in11(x11q_t), .in12(x12q_t), .in13(x13q_t),
    .in14(x14q_t), .in15(x15q_t), .in16(x16q_t), .in17(x17q_t), .in18(x18q_t), .in19(x19q_t), .in20(x20q_t),
    .in21(x21q_t), .in22(x22q_t), .in23(x23q_t), .in24(x24q_t), .in25(x25q_t), .in26(x26q_t), .in27(x27q_t),
    .in28(x28q_t), .in29(x29q_t), .in30(x30q_t), .in31(x31q_t), .out(rs2), .sel(rsi2));
  Multiplexer #(.select(5), .width(32)) multiplexer_2 (
    .in0({32{1'b0}}), .in1(x1q_t), .in2(x2q_t), .in3(x3q_t), .in4(x4q_t), .in5(x5q_t), .in6(x6q_t),
    .in7(x7q_t), .in8(x8q_t), .in9(x9q_t), .in10(x10q_t), .in11(x11q_t), .in12(x12q_t), .in13(x13q_t),
    .in14(x14q_t), .in15(x15q_t), .in16(x16q_t), .in17(x17q_t), .in18(x18q_t), .in19(x19q_t), .in20(x20q_t),
    .in21(x21q_t), .in22(x22q_t), .in23(x23q_t), .in24(x24q_t), .in25(x25q_t), .in26(x26q_t), .in27(x27q_t),
    .in28(x28q_t), .in29(x29q_t), .in30(x30q_t), .in31(x31q_t), .out(rs1), .sel(rsi1));

  // Other names for the same wires on the sheet: CLK_t = CLK; rd_t[31:0] = rd; rdi_t[4:0] = rdi; rs1_t[31:0] = rs1;
  //   rs2_t[31:0] = rs2; rsi1_t[4:0] = rsi1; rsi2_t[4:0] = rsi2; we_t = we

  // Notes on the sheet:
  //   Register Destination Index
  //   Register Destination Value
  //   Write Enable
  //   Clock
  //   Register Source Index
  //   si x0we enciende, es falta
  //   x0 siempre es 0
  //   Output Register Values
endmodule

module InmExtractor (
  input  [31:0] instr,
  output [31:0] I_imm,
  output [31:0] S_imm,
  output [31:0] B_imm,
  output [31:0] U_imm,
  output [31:0] J_imm
);

  // NoConnect on instr[6:0]
  assign {I_imm[31], B_imm[31:12]} = {{20{instr[31]}}, instr[31]};  // Bit_Extender bit_extender_1
  // NoConnect on I_imm[31]
  // NoConnect on {I_imm[31], B_imm[31:13]}
  // NoConnect on {I_imm[31], B_imm[31:24]}

  assign B_imm[11:0] = {instr[7], instr[30:25], instr[11:8], 1'b0};
  assign I_imm[30:0] = {B_imm[31:12], instr[30:20]};
  assign J_imm = {B_imm[23:12], instr[19:12], instr[20], instr[30:21], 1'b0};
  assign S_imm = {I_imm[31], B_imm[31:12], instr[30:25], instr[11:7]};
  assign U_imm = {B_imm[12], instr[30:12], {12{1'b0}}};

  // Notes on the sheet:
  //   I-imm
  //   S-imm
  //   B-imm
  //   U-imm
  //   J-imm
endmodule

module IDecode (
  input  [31:0] instr,
  output [4:0] rd,
  output [2:0] funct3,
  output [4:0] rs1,
  output [4:0] rs2,
  output [6:0] funct7,
  output [31:0] imm,
  output ar_r,
  output ar_i,
  output ld,
  output st,
  output br,
  output jal,
  output jalr,
  output lui,
  output auipc,
  output ebc
);

  wire or_1_out;
  wire [31:0] inmextractor_1_b_imm, inmextractor_1_i_imm, inmextractor_1_j_imm, inmextractor_1_s_imm,
       inmextractor_1_u_imm, multiplexer_1_out, multiplexer_2_out, multiplexer_3_out;

  Comparator #(.width(7)) comparator_1 (.a(instr[6:0]), .b(7'b0110011), .eq(ar_r));  // open: gt, lt
  Comparator #(.width(7)) comparator_2 (.a(instr[6:0]), .b(7'b0010011), .eq(ar_i));  // open: gt, lt
  Comparator #(.width(7)) comparator_3 (.a(instr[6:0]), .b(7'b0000011), .eq(ld));  // open: gt, lt
  Comparator #(.width(7)) comparator_4 (.a(instr[6:0]), .b(7'b0100011), .eq(st));  // open: gt, lt
  Comparator #(.width(7)) comparator_5 (.a(instr[6:0]), .b(7'b1100011), .eq(br));  // open: gt, lt
  Comparator #(.width(7)) comparator_6 (.a(instr[6:0]), .b(7'b1101111), .eq(jal));  // open: gt, lt
  Comparator #(.width(7)) comparator_7 (.a(instr[6:0]), .b(7'b1100111), .eq(jalr));  // open: gt, lt
  Comparator #(.width(7)) comparator_8 (.a(instr[6:0]), .b(7'b0110111), .eq(lui));  // open: gt, lt
  Comparator #(.width(7)) comparator_9 (.a(instr[6:0]), .b(7'b0010111), .eq(auipc));  // open: gt, lt
  Comparator #(.width(7)) comparator_10 (.a(instr[6:0]), .b(7'b1110011), .eq(ebc));  // open: gt, lt
  InmExtractor inmextractor_1 (
    .instr(instr), .I_imm(inmextractor_1_i_imm), .S_imm(inmextractor_1_s_imm), .B_imm(inmextractor_1_b_imm),
    .U_imm(inmextractor_1_u_imm), .J_imm(inmextractor_1_j_imm));
  Multiplexer #(.width(32)) multiplexer_1 (
    .in0(inmextractor_1_i_imm), .in1(inmextractor_1_s_imm), .out(multiplexer_1_out), .sel(st));
  Multiplexer #(.width(32)) multiplexer_2 (
    .in0(multiplexer_1_out), .in1(inmextractor_1_b_imm), .out(multiplexer_2_out), .sel(br));
  Multiplexer #(.width(32)) multiplexer_3 (
    .in0(multiplexer_2_out), .in1(inmextractor_1_u_imm), .out(multiplexer_3_out), .sel(or_1_out));
  or or_1 (or_1_out, auipc, lui);
  Multiplexer #(.width(32)) multiplexer_4 (.in0(multiplexer_3_out), .in1(inmextractor_1_j_imm), .out(imm), .sel(jal));

  assign funct3 = instr[14:12];
  assign funct7 = instr[31:25];
  assign rd = instr[11:7];
  assign rs1 = instr[19:15];
  assign rs2 = instr[24:20];
endmodule

// VHDL entity ALU, as the project stores it:
LIBRARY ieee;
USE ieee.std_logic_1164.all;

ENTITY ALU IS
  PORT (
  ------------------------------------------------------------------------------
  --Insert input ports below
    clock      : IN  std_logic;                    -- input bit example
    val        : IN  std_logic_vector(3 DOWNTO 0); -- input vector example
  ------------------------------------------------------------------------------
  --Insert output ports below
    max        : OUT std_logic;                    -- output bit example
    cpt        : OUT std_logic_vector(3 DOWNTO 0)  -- output vector example
    );
END ALU;

--------------------------------------------------------------------------------
--Complete your VHDL description below
--------------------------------------------------------------------------------

ARCHITECTURE TypeArchitecture OF ALU IS

BEGIN


END TypeArchitecture;
